# Fritzing sketch Differential Op Amp (saved by Fritzing 0.9.3b)
breadboards: 1

parts:
  U1 = LM 358 Dual Op-Amp [package="SO 08 [SMD]"]
  Part1 = Arduino Uno (Rev3)
  R1 = Resistor [tolerance=±5% resistance=220 package=THT]
  R2 = Resistor [tolerance=±5% resistance=220 package=THT]
  R3 = Resistor [tolerance=±5% resistance=220 package=THT]
  R4 = Resistor [tolerance=±5% resistance=220 package=THT]

nets:
  N1: U1.connector0, R2.Pin_1
  N2: U1.connector1, R1.Pin_1, R2.Pin_0
  N3: U1.connector2, R3.Pin_1, R4.Pin_0
  N4: Part1.GND, R4.Pin_1
  N5: Part1.5V, R1.Pin_0, R3.Pin_0
