# Fritzing sketch Fading_Fritzing (saved by Fritzing 0.9.3b)
breadboards: 2

parts:
  Part1 = Arduino Uno (Rev3)
  LED1 = LED - 5mm [color="Red (633nm)" package="5 mm [THT]"]
  LED2 = LED - 5mm [color="White (4500K)" package="5 mm [THT]"]
  LED3 = LED - 5mm [color="Yellow (592nm)" package="5 mm [THT]"]
  LED4 = LED - 5mm [color="Green (555nm)" package="5 mm [THT]"]
  LED5 = LED - 5mm [color="Blue (470nm)" package="5 mm [THT]"]
  R1 = Resistor [tolerance=±5% resistance=220 package=THT]
  R2 = Resistor [tolerance=±5% resistance=220 package=THT]
  R3 = Resistor [tolerance=±5% resistance=220 package=THT]
  R4 = Resistor [tolerance=±5% resistance=220 package=THT]
  R5 = Resistor [tolerance=±5% resistance=220 package=THT]
  J1 = Piezo Speaker
  R6 = Photocell (LDR) [package=THT]

nets (from the breadboard view):
  N1: Part1.A0, J1.pin2, R6.pin_1
  N2: Part1.D9_PWM, LED4.anode
  N3: Part1.D10_PWM/SS, LED3.anode
  N4: Part1.D11_PWM/MOSI, LED1.anode
  N5: Part1.GND, R1.Pin_1, R2.Pin_1, R3.Pin_1, R4.Pin_1, R5.Pin_1, J1.pin1
  N6: Part1.D3_PWM, R6.pin_0
  N7: Part1.D5_PWM, LED2.anode
  N8: Part1.D6_PWM, LED5.anode
  N9: LED1.cathode, R1.Pin_0
  N10: LED2.cathode, R2.Pin_0
  N11: LED3.cathode, R5.Pin_0
  N12: LED4.cathode, R3.Pin_0
  N13: LED5.cathode, R4.Pin_0
