# Fritzing sketch FinalProject_Fritzing (saved by Fritzing 0.9.3b)
breadboards: 2

parts:
  Part1 = Arduino Uno (Rev3)
  LED1 = LED - 5mm [color="Red (633nm)" package="5 mm [THT]"]
  LED2 = LED - 5mm [color="White (4500K)" package="5 mm [THT]"]
  LED3 = LED - 5mm [color="Yellow (592nm)" package="5 mm [THT]"]
  LED4 = LED - 5mm [color="Green (555nm)" package="5 mm [THT]"]
  LED5 = LED - 5mm [color="Blue (470nm)" package="5 mm [THT]"]
  R1 = Resistor [tolerance=±5% resistance=220 package=THT]
  R2 = Resistor [tolerance=±5% resistance=220 package=THT]
  R3 = Resistor [tolerance=±5% resistance=220 package=THT]
  R4 = Resistor [tolerance=±5% resistance=220 package=THT]
  R5 = Resistor [tolerance=±5% resistance=220 package=THT]
  J1 = Piezo Speaker
  R6 = Photocell (LDR) [package=THT]
  Part2 = Arduino Mega 2560 (Rev3)
  R7 = Resistor [tolerance=±5% resistance=220 package=THT]
  R8 = Photocell (LDR) [package=THT]
  LED6 = RGB LED (com. cathode, rgb) [package="5 mm [THT]"]
  R9 = Resistor [tolerance=±5% resistance=220 package=THT]
  R10 = Resistor [tolerance=±5% resistance=220 package=THT]
  R11 = Resistor [tolerance=±5% resistance=220 package=THT]
  J2 = Infrared Proximity Sensor
  LED7 = LED - 5mm [color="Red (633nm)" package="5 mm [THT]"]
  R12 = Resistor [tolerance=±5% resistance=220 package=THT]
  J3 = Piezo Speaker

nets (from the breadboard view):
  N1: Part1.A0, J1.pin2, R6.pin_1
  N2: Part1.D9_PWM, LED4.anode
  N3: Part1.D10_PWM/SS, LED3.anode
  N4: Part1.D11_PWM/MOSI, LED1.anode
  N5: Part1.GND, R1.Pin_1, R2.Pin_1, R3.Pin_1, R4.Pin_1, R5.Pin_1, J1.pin1
  N6: Part1.D3_PWM, R6.pin_0
  N7: Part1.D5_PWM, LED2.anode
  N8: Part1.D6_PWM, LED5.anode
  N9: LED1.cathode, R1.Pin_0
  N10: LED2.cathode, R2.Pin_0
  N11: LED3.cathode, R5.Pin_0
  N12: LED4.cathode, R3.Pin_0
  N13: LED5.cathode, R4.Pin_0
  N14: Part2.A0, R7.Pin_0, R8.pin_1
  GND: Part2.GND, R7.Pin_1, J2.GND, R12.Pin_1, J3.pin1
  5V: Part2.5V, R8.pin_0, LED6.common_cathode, J2.Vcc, LED7.anode, J3.pin2
  N15: Part2.D2_PWM, R9.Pin_0
  N16: Part2.D3_PWM, J2.Vout
  N17: Part2.D4_PWM, R10.Pin_0
  N18: Part2.D6_PWM, R11.Pin_0
  N19: LED6.red_anode, R9.Pin_1
  N20: LED6.green_anode, R10.Pin_1
  N21: LED6.blue_anode, R11.Pin_1
  N22: LED7.cathode, R12.Pin_0
